// Logisim project lab1part1.circ as structural Verilog: 1 circuit, main circuit main
module main (
  input  y,
  input  s,
  input  x,
  output f
);

  wire n7404_1_p2, n7408_1_p3, n7432_1_p1;

  // _7404 7404_1: pin names not known; wires that end beside it: s, n7404_1_p2
  // _7408 7408_1: pin names not known; wires that end beside it: y, s, n7408_1_p3, n7404_1_p2, x
  // _7432 7432_1: pin names not known; wires that end beside it: n7432_1_p1, n7408_1_p3, n7432_1_p1, f
endmodule
